# Fritzing sketch Schema (saved by Fritzing 0.9.2b)

parts:
  LED1 = DUO LED RG [package="5 mm [THT]"]
  Composant1 = Arduino Nano (Rev3.0) (ICSP)
  S1 = Momentary Switch [package=ksa_sealed_tac_switch]
  Raspberry_Pi1 = Raspberry Pi B+
  R4 = Resistor [tolerance=±5% resistance=10k package=THT]
  R5 = Trimmer Potentiometer [maximum_resistance=10kΩ package=THT]
  U7 = RELAY [package=relay-jzc]
  U8 = RELAY [package=relay-jzc]
  U9 = mystery part, 18 pins [chip_label="Keyboard connector"]

nets:
  N1: LED1.red_anode, Composant1.D11/MOSI
  N2: LED1.green_anode, Composant1.D10
  GND: Composant1.GND, Raspberry_Pi1.GND
  N3: Composant1.D5, U7.NC
  N4: Composant1.D6, U8.NC
  N5: Composant1.D12/MISO, S1.2, R4.Pin_0
  N6: Composant1.A5, Raspberry_Pi1.GPIO3
  N7: Composant1.A4, Raspberry_Pi1.GPIO2, Raspberry_Pi1.5V
  N8: Composant1.A0, R5.wiper
  N9: Raspberry_Pi1.GPIO4, U9.pin2
  N10: Raspberry_Pi1.GPIO17, U9.pin4
  N11: Raspberry_Pi1.GPIO27, U9.pin5
  N12: Raspberry_Pi1.GPIO22, U9.pin7
  N13: Raspberry_Pi1.GPIO5, U9.pin10
  N14: Raspberry_Pi1.GPIO6, U9.pin12
  N15: Raspberry_Pi1.GPIO13, U9.pin13
  N16: Raspberry_Pi1.GPIO19, U9.pin15
  N17: Raspberry_Pi1.GPIO26, U9.pin18
  N18: Raspberry_Pi1.GPIO21, U9.pin17
  N19: Raspberry_Pi1.GPIO20, U9.pin16
  N20: Raspberry_Pi1.GPIO16, U9.pin14
  N21: Raspberry_Pi1.GPIO12, U9.pin11
  N22: Raspberry_Pi1.GPIO25, U9.pin9
  N23: Raspberry_Pi1.GPIO24, U9.pin8
  N24: Raspberry_Pi1.GPIO23, U9.pin6
  N25: Raspberry_Pi1.GPIO18, U9.pin3
  N26: Raspberry_Pi1.GPIO14, U9.pin1

notes:
  I2C : shutdown ->
  volume ->
  ready <-
  Yellow SDA
  Brown SCL
  Volume
  On/Off
  Status LED
  /!\ Connect grounds
  Keyboard
  Relay 5V
  Relay 12V
  SUPER SWAG MINITEL
  Logical view - March 2017
