# Fritzing sketch Schema (saved by Fritzing 0.9.2b)

parts:
  Q2 = TRANSISTOR_NPN [package=to-92-ammo]
  U1 = Optocoupler [package=THT]
  LED1 = DUO LED RG [package="5 mm [THT]"]
  Composant1 = Arduino Nano (Rev3.0) (ICSP)
  S1 = Momentary Switch [package=ksa_sealed_tac_switch]
  U2 = mystery part, 2 pins [chip_label=5V]
  U3 = mystery part, 2 pins [chip_label=12V]
  U5 = mystery part, 2 pins [chip_label=?]
  Q5 = TRANSISTOR_NPN [package=to-92-ammo]
  R3 = Resistor [tolerance=±5% resistance=10k package=THT]
  Raspberry_Pi1 = Raspberry Pi B+
  R4 = Resistor [tolerance=±5% resistance=10k package=THT]
  R5 = Trimmer Potentiometer [maximum_resistance=10kΩ package=THT]
  R6 = Resistor [tolerance=±5% resistance=230k package=THT]

nets:
  N1: Q2.B, Composant1.D3
  N2: Q2.C, U2.pin1
  N3: U1.Pin_1, R6.Pin_0
  N4: U1.Pin_4, U3.pin1
  N5: U1.Pin_5, U5.pin2
  N6: LED1.red_anode, Composant1.D11/MOSI
  N7: LED1.green_anode, Composant1.D10
  GND: Composant1.GND, Q5.C, Raspberry_Pi1.GND
  N8: Composant1.D4, R6.Pin_1
  N9: Composant1.D8, S1.1
  N10: Composant1.A5, Raspberry_Pi1.GPIO3
  N11: Composant1.A4, Raspberry_Pi1.GPIO2
  N12: Composant1.A1, R5.wiper
  N13: S1.2, R4.Pin_0
  N14: U3.pin2, U5.pin1
  N15: Q5.E, R3.Pin_1
  N16: Q5.B, Raspberry_Pi1.GPIO14

notes:
  Alim 5V
  Alim 12V
  Carte fille Ecran LCD
  I2C : shutdown ->
  volume ->
  ready <-
  Volume
  On/Off
  LED d'état
  Run
  Relie les -
